// Logisim project mux.circ as structural Verilog: 17 circuits, main circuit mux2
module mux2 (
  input  I0,
  input  I1,
  input  Sel,
  output out_4
);

  wire and_1_out, and_2_out;

  and and_1 (and_1_out, I0, ~Sel);  // AND_Gate
  and and_2 (and_2_out, I1, Sel);
  or or_1 (out_4, and_1_out, and_2_out);
endmodule

module mux2_4bits (
  input  [3:0] I0,
  input  [3:0] I1,
  input  in_3,
  output [3:0] out_4
);

  wire [3:0] and_1_out, and_2_out;

  assign and_1_out = I0 & ~{4{in_3}};  // AND_Gate and_1, 4 bits wide
  assign and_2_out = I1 & {4{in_3}};  // AND_Gate and_2, 4 bits wide
  assign out_4 = and_1_out | and_2_out;  // OR_Gate or_1, 4 bits wide
endmodule

module mux4 (
  input  l0,
  input  l1,
  input  l2,
  input  l3,
  input  sel1,
  input  sel0,
  output out_7
);

  wire mux2_1_out_4, mux2_2_out_4;

  mux2 mux2_1 (.I0(l0), .I1(l1), .Sel(sel0), .out_4(mux2_1_out_4));
  mux2 mux2_2 (.I0(l2), .I1(l3), .Sel(sel0), .out_4(mux2_2_out_4));
  mux2 mux2_3 (.I0(mux2_1_out_4), .I1(mux2_2_out_4), .Sel(sel1), .out_4(out_7));
endmodule

module mux4b (
  input  l0,
  input  l1,
  input  l2,
  input  l3,
  input  [1:0] in_5,
  output out_6
);

  wire mux2_1_out_4, mux2_2_out_4;

  mux2 mux2_1 (.I0(l0), .I1(l1), .Sel(in_5[0]), .out_4(mux2_1_out_4));
  mux2 mux2_2 (.I0(l2), .I1(l3), .Sel(in_5[0]), .out_4(mux2_2_out_4));
  mux2 mux2_3 (.I0(mux2_1_out_4), .I1(mux2_2_out_4), .Sel(in_5[1]), .out_4(out_6));
endmodule

module mux8 (
  input  l0,
  input  l1,
  input  l2,
  input  l3,
  input  l4,
  input  l5,
  input  l6,
  input  l7,
  input  sel2,
  input  sel1,
  input  sel0,
  output out_12
);

  wire mux4_1_out_7, mux4_2_out_7;

  mux4 mux4_1 (.l0(l0), .l1(l1), .l2(l2), .l3(l3), .sel1(sel1), .sel0(sel0), .out_7(mux4_1_out_7));
  mux4 mux4_2 (.l0(l4), .l1(l5), .l2(l6), .l3(l7), .sel1(sel1), .sel0(sel0), .out_7(mux4_2_out_7));
  mux2 mux2_1 (.I0(mux4_1_out_7), .I1(mux4_2_out_7), .Sel(sel2), .out_4(out_12));
endmodule

module mux8b (
  input  l0,
  input  l1,
  input  l2,
  input  l3,
  input  l4,
  input  l5,
  input  l6,
  input  l7,
  input  [2:0] sel,
  output out_10
);

  wire mux4_1_out_7, mux4_2_out_7;

  mux4 mux4_1 (.l0(l0), .l1(l1), .l2(l2), .l3(l3), .sel1(sel[1]), .sel0(sel[0]), .out_7(mux4_1_out_7));
  mux4 mux4_2 (.l0(l4), .l1(l5), .l2(l6), .l3(l7), .sel1(sel[1]), .sel0(sel[0]), .out_7(mux4_2_out_7));
  mux2 mux2_1 (.I0(mux4_1_out_7), .I1(mux4_2_out_7), .Sel(sel[2]), .out_4(out_10));
endmodule

module mux16 (
  input  l0,
  input  l1,
  input  l2,
  input  l3,
  input  l4,
  input  l5,
  input  l6,
  input  l7,
  input  l8,
  input  l9,
  input  l10,
  input  l11,
  input  l12,
  input  l13,
  input  l14,
  input  l15,
  input  sel3,
  input  sel2,
  input  sel1,
  input  sel0,
  output out_21
);

  wire mux8_1_out_12, mux8_2_out_12;

  mux8 mux8_1 (
    .l0(l0), .l1(l1), .l2(l2), .l3(l3), .l4(l4), .l5(l5), .l6(l6), .l7(l7), .sel2(sel2), .sel1(sel1),
    .sel0(sel0), .out_12(mux8_1_out_12));
  mux8 mux8_2 (
    .l0(l8), .l1(l9), .l2(l10), .l3(l11), .l4(l12), .l5(l13), .l6(l14), .l7(l15), .sel2(sel2), .sel1(sel1),
    .sel0(sel0), .out_12(mux8_2_out_12));
  mux2 mux2_1 (.I0(mux8_1_out_12), .I1(mux8_2_out_12), .Sel(sel3), .out_4(out_21));
endmodule

module mux32 (
  input  l0,
  input  l1,
  input  l2,
  input  l3,
  input  l4,
  input  l5,
  input  l6,
  input  l7,
  input  l8,
  input  l9,
  input  l10,
  input  l11,
  input  l12,
  input  l13,
  input  l14,
  input  l15,
  input  l16,
  input  l17,
  input  l18,
  input  l19,
  input  l20,
  input  l21,
  input  l22,
  input  l23,
  input  l24,
  input  l25,
  input  l26,
  input  l27,
  input  l28,
  input  l29,
  input  l30,
  input  sel5,
  input  sel3,
  input  sel2,
  input  sel1,
  input  sel0,
  input  l31,
  output out_38
);

  wire mux16_1_out_21, mux16_2_out_21;

  mux16 mux16_1 (
    .l0(l0), .l1(l1), .l2(l2), .l3(l3), .l4(l4), .l5(l5), .l6(l6), .l7(l7), .l8(l8), .l9(l9), .l10(l10),
    .l11(l11), .l12(l12), .l13(l13), .l14(l14), .l15(l15), .sel3(sel3), .sel2(sel2), .sel1(sel1),
    .sel0(sel0), .out_21(mux16_1_out_21));
  mux16 mux16_2 (
    .l0(l16), .l1(l17), .l2(l18), .l3(l19), .l4(l20), .l5(l21), .l6(l22), .l7(l23), .l8(l24), .l9(l25),
    .l10(l26), .l11(l27), .l12(l28), .l13(l29), .l14(l30), .l15(l31), .sel3(sel3), .sel2(sel2), .sel1(sel1),
    .sel0(sel0), .out_21(mux16_2_out_21));
  mux2 mux2_1 (.I0(mux16_1_out_21), .I1(mux16_2_out_21), .Sel(sel5), .out_4(out_38));
endmodule

module somador (
  input  vem1,
  input  B,
  input  A,
  output soma,
  output vai1
);

  wire and_1_out, and_2_out, and_3_out, and_4_out, or_1_out, xnor_1_out, xor_1_out;

  xor xor_1 (xor_1_out, B, A);
  or or_1 (or_1_out, B, A);
  xnor xnor_1 (xnor_1_out, B, A);
  and and_1 (and_1_out, B, A);
  and and_2 (and_2_out, or_1_out, vem1);
  and and_3 (and_3_out, xnor_1_out, vem1);
  and and_4 (and_4_out, xor_1_out, ~vem1);  // AND_Gate
  or or_2 (vai1, and_1_out, and_2_out);
  or or_3 (soma, and_3_out, and_4_out);
endmodule

module somador16 (
  input  [15:0] A,
  input  [15:0] B,
  output [15:0] out_3
);

  wire somador_1_p4, somador_2_p6, somador_3_p6, somador_4_p6, somador_5_p2, somador_5_p6, somador_7_p2,
       somador_7_p6, somador_9_p6, somador_10_p2, somador_10_p6, somador_12_p6, somador_13_p6, somador_14_p6,
       somador_15_p6;

  // somador somador_1: pin names not known; wires that end beside it: A[15], out_3[15], B[15], somador_1_p4
  // somador somador_2: pin names not known; wires that end beside it: B[15], somador_1_p4, A[14], out_3[14], B[14], somador_2_p6
  // somador somador_3: pin names not known; wires that end beside it: B[14], somador_2_p6, A[13], out_3[13], B[13], somador_3_p6
  // somador somador_4: pin names not known; wires that end beside it: B[13], somador_3_p6, A[12], out_3[12], B[12], somador_4_p6
  // somador somador_5: pin names not known; wires that end beside it: B[11], somador_5_p2, A[10], out_3[10], B[10], somador_5_p6
  // somador somador_6: pin names not known; wires that end beside it: B[12], somador_4_p6, A[11], out_3[11], B[11], somador_5_p2
  // somador somador_7: pin names not known; wires that end beside it: B[9], somador_7_p2, A[8], out_3[8], B[8], somador_7_p6
  // somador somador_8: pin names not known; wires that end beside it: B[10], somador_5_p6, A[9], out_3[9], B[9], somador_7_p2
  // somador somador_9: pin names not known; wires that end beside it: B[8], somador_7_p6, A[7], out_3[7], B[7], somador_9_p6
  // somador somador_10: pin names not known; wires that end beside it: B[6], somador_10_p2, A[5], out_3[5], B[5], somador_10_p6
  // somador somador_11: pin names not known; wires that end beside it: B[7], somador_9_p6, A[6], out_3[6], B[6], somador_10_p2
  // somador somador_12: pin names not known; wires that end beside it: B[5], somador_10_p6, A[4], out_3[4], B[4], somador_12_p6
  // somador somador_13: pin names not known; wires that end beside it: B[4], somador_12_p6, A[3], out_3[3], B[3], somador_13_p6
  // somador somador_14: pin names not known; wires that end beside it: B[3], somador_13_p6, A[2], out_3[2], B[2], somador_14_p6
  // somador somador_15: pin names not known; wires that end beside it: B[2], somador_14_p6, A[1], out_3[1], B[1], somador_15_p6
  // somador somador_16: pin names not known; wires that end beside it: B[1], somador_15_p6, A[0], out_3[0], B[0], 1'b0
endmodule

module ShiftLeftLogical (
  input  [3:0] in_1,
  input  shift,
  output [3:0] out_3
);

  mux2_4bits mux2_4bits_1 (.I0(in_1), .I1({in_1[2:0], 1'b0}), .in_3(shift), .out_4(out_3));

  // Notes on the sheet:
  //   Deslocar para esquerda é o mesmo que multiplicar por 2
endmodule

module ShiftRightLogical (
  input  [3:0] in_1,
  input  in_2,
  output [3:0] out_3
);

  mux2_4bits mux2_4bits_1 (.I0(in_1), .I1({1'b0, in_1[3:1]}), .in_3(in_2), .out_4(out_3));

  // Notes on the sheet:
  //   Deslocar para direita é o mesmo que dividir por 2
endmodule

module ShiftLeftArith (
  input  [3:0] in_1,
  input  in_2,
  output [3:0] out_3
);

  mux2_4bits mux2_4bits_1 (.I0(in_1), .I1({in_1[2:0], in_1[0]}), .in_3(in_2), .out_4(out_3));
endmodule

module ShiftRightArith (
  input  [3:0] in_1,
  input  in_2,
  output [3:0] out_3
);

  mux2_4bits mux2_4bits_1 (.I0(in_1), .I1({{2{in_1[3]}}, in_1[2:1]}), .in_3(in_2), .out_4(out_3));
endmodule

module UlaCell (
  input  a,
  input  b,
  input  vem1,
  input  [2:0] OpCode,
  output saida,
  output vai1
);

  wire and_1_out, or_1_out, somador_1_soma, xor_1_out;

  and and_1 (and_1_out, b, a);
  or or_1 (or_1_out, b, a);
  somador somador_1 (.B(b), .A(a), .vem1(vem1), .vai1(vai1), .soma(somador_1_soma));
  xor xor_1 (xor_1_out, b, a);
  mux8b mux8b_1 (
    .l0(and_1_out), .l1(or_1_out), .l2(somador_1_soma), .l3(xor_1_out), .l4(a), .l5(b), .sel(OpCode),
    .out_10(saida));  // open: l6, l7
endmodule

module ULA (
  input  [3:0] A,
  input  [3:0] B,
  input  [2:0] UlaOpCode,
  output [3:0] out_4
);

  wire slldetector_1_saida, ulacell_2_vai1, ulacell_3_vai1, ulacell_4_vai1;
  wire [3:0] shiftleftlogical_1_out_3;

  ShiftLeftLogical shiftleftlogical_1 (.in_1(B), .shift(slldetector_1_saida), .out_3(shiftleftlogical_1_out_3));
  SLLDetector slldetector_1 (.saida(slldetector_1_saida), .UlaOpCode(UlaOpCode));
  UlaCell ulacell_1 (
    .a(A[3]), .b(shiftleftlogical_1_out_3[3]), .OpCode(UlaOpCode), .saida(out_4[3]), .vem1(ulacell_2_vai1));  // open: vai1
  UlaCell ulacell_2 (
    .vai1(ulacell_2_vai1), .a(A[2]), .b(shiftleftlogical_1_out_3[2]), .OpCode(UlaOpCode), .saida(out_4[2]),
    .vem1(ulacell_3_vai1));
  UlaCell ulacell_3 (
    .vai1(ulacell_3_vai1), .a(A[1]), .b(shiftleftlogical_1_out_3[1]), .OpCode(UlaOpCode), .saida(out_4[1]),
    .vem1(ulacell_4_vai1));
  UlaCell ulacell_4 (
    .vai1(ulacell_4_vai1), .a(A[0]), .b(shiftleftlogical_1_out_3[0]), .OpCode(UlaOpCode), .saida(out_4[0]),
    .vem1(1'b0));

  // Notes on the sheet:
  //   000 - AND
  //   001 - OR
  //   010 - SOMADOR
  //   011 - XOR
  //   100 - SLL A
  //   101 - SLL B
endmodule

module SLLDetector (
  input  [2:0] UlaOpCode,
  output saida
);

  and and_1 (saida, UlaOpCode[0], ~UlaOpCode[1], UlaOpCode[2]);  // AND_Gate
endmodule
